# Fritzing sketch TestingCircuit (saved by Fritzing 0.9.3b)
breadboards: 1

parts:
  Mod1 = Heltec WiFi Kit 32 [part_number=HTIT-WB32LA]
  S1 = Momentary Switch 6mm 2pin
  S2 = Momentary Switch 6mm 2pin
  R6 = Rotary Potentiometer (Small) [maximum_resistance=100kΩ package=THT]
  R7 = Resistor [tolerance=±5% resistance=220 package="2512 [SMD]"]
  R8 = Resistor [tolerance=±5% resistance=220 package="0402 [SMD]"]
  LED3 = smd LED [color="Green (555nm)" package="0805 [SMD]"]
  R9 = Resistor [tolerance=±5% resistance=220 package="0402 [SMD]"]

nets:
  N1: Mod1.pin_1, LED3.cathode
  N2: Mod1.pin_15, Mod1.pin_18, Mod1.pin_19
  N3: Mod1.pin_16, Mod1.pin_21, R8.Pin_1, R9.Pin_1
  N4: Mod1.pin_17, Mod1.pin_20
  N5: Mod1.pin_23, S1.1
  N6: Mod1.pin_24, S2.1
  N7: Mod1.pin_36, R6.wiper
  N8: S1.2, R9.Pin_0
  N9: S2.2, R8.Pin_0
  N10: R6.leg1, R7.Pin_0
  N11: R7.Pin_1, LED3.anode

custom parts:
  Heltec WiFi Kit 32: Heltec WiFi Kit 32 WiFi Kit 32 is a classic IoT dev-board designed & produced by Heltec Automation(TM). It’s a highly integrated product based on ESP32 + SX127x, it has Wi-Fi, BLE, LoRa functions, also Li-Po battery management system, 0.96″ OLED are also included. It’s the best choice for smart cities, smart farms, smart home, and IoT makers.
  Momentary Switch 6mm 2pin: Momentary Switch 6mm 2 pin Button commonly used for reset or general input.
